# Fritzing sketch Vfo Wiring (saved by Fritzing 0.9.2b)
breadboards: 1

parts:
  Part1 = Arduino Uno (Rev3)
  U1 = LCD-16X2 [package=lcd-16x2]
  S1 = Pushbutton [package=THT]
  S2 = Pushbutton [package=THT]
  S3 = Pushbutton [package=THT]
  R1 = Trimmer Potentiometer [maximum_resistance=10kΩ package=THT]

nets:
  N1: Part1.D8, U1.E
  N2: Part1.D9_PWM, U1.DB4
  N3: Part1.D10_PWM/SS, U1.DB5
  N4: Part1.D11_PWM/MOSI, U1.DB6
  N5: Part1.D12/MISO, U1.DB7
  GND: Part1.GND, U1.VSS, S1.leg0, S2.leg0, S3.leg0, R1.wiper
  N6: Part1.D4, S3.leg1
  N7: Part1.D5_PWM, S1.leg1
  N8: Part1.D6_PWM, S2.leg1
  N9: Part1.D7, U1.RS
  5V: Part1.5V, U1.VDD
  N10: U1.A, R1.leg2
  N11: U1.K, R1.leg1
